// Logisim project Secuencias_minimizado.circ as structural Verilog: 12 circuits, main circuit main
module main (
  input  CLK,
  input  X,
  output S1,
  output S2,
  output S3
);

  wire CLEAR_out, Q0, Q1, Q2, Q3, R0, R1, R2, R3, S0, S1_t, S2_t, S3_t;

  S3_Simplificado s3_simplificado_1 (.Q3(Q3), .Q2(Q2), .Q1(Q1), .Q0(Q0), .S3(S3_t));
  R3_Simplificado r3_simplificado_1 (.Q3(Q3), .Q2(Q2), .Q1(Q1), .Q0(Q0), .X(X), .R3(R3));
  S2_Simplificado s2_simplificado_1 (.Q3(Q3), .Q2(Q2), .Q1(Q1), .Q0(Q0), .X(X), .S2(S2_t));
  R2_Simplificado r2_simplificado_1 (.Q3(Q3), .Q2(Q2), .Q1(Q1), .Q0(Q0), .X(X), .R2(R2));
  S1_Simplificado s1_simplificado_1 (.Q3(Q3), .Q2(Q2), .Q1(Q1), .Q0(Q0), .X(X), .S1(S1_t));
  R1_Simplificado r1_simplificado_1 (.Q3(Q3), .Q2(Q2), .Q1(Q1), .Q0(Q0), .X(X), .R1(R1));
  S0_Simplificado s0_simplificado_1 (.Q3(Q3), .Q2(Q2), .Q1(Q1), .Q0(Q0), .X(X), .S0(S0));
  R0_Simplificado r0_simplificado_1 (.Q3(Q3), .Q2(Q2), .Q1(Q1), .Q0(Q0), .X(X), .R0(R0));
  Button CLEAR (.out(CLEAR_out));
  Z1_Simplificado z1_simplificado_1 (.Q3(Q3), .Q2(Q2), .Q0(Q0), .Z1(S1));
  Z2_Simplificado z2_simplificado_1 (.Q3(Q3), .Q2(Q2), .Q1(Q1), .Q0(Q0), .out_5(S2));
  Z3_Simplificado z3_simplificado_1 (.Q3(Q3), .Q2(Q2), .Q1(Q1), .Q0(Q0), .Z3(S3));
  S_R_Flip_Flop SR3 (.S(S3_t), .R(R3), .clk(CLK), .Q(Q3), .reset(CLEAR_out));  // open: Qn, preset
  S_R_Flip_Flop SR2 (.S(S2_t), .R(R2), .clk(CLK), .Q(Q2), .reset(CLEAR_out));  // open: Qn, preset
  S_R_Flip_Flop SR1 (.S(S1_t), .R(R1), .clk(CLK), .Q(Q1), .reset(CLEAR_out));  // open: Qn, preset
  S_R_Flip_Flop SR0 (.S(S0), .R(R0), .clk(CLK), .Q(Q0), .reset(CLEAR_out));  // open: Qn, preset
endmodule

module S3_Simplificado (
  input  Q3,
  input  Q2,
  input  Q1,
  input  Q0,
  output S3
);

  wire not_1_out, not_2_out;

  not not_1 (not_1_out, Q3);
  not not_2 (not_2_out, Q1);
  and and_1 (S3, not_1_out, Q2, not_2_out, Q0);
endmodule

module R3_Simplificado (
  input  Q3,
  input  Q2,
  input  Q1,
  input  Q0,
  input  X,
  output R3
);

  wire and_1_out, and_2_out, and_3_out, not_1_out, not_2_out, or_1_out;

  not not_1 (not_1_out, Q0);
  not not_2 (not_2_out, X);
  and and_1 (and_1_out, Q3, Q2, Q0, X);
  and and_2 (and_2_out, Q2, Q1, not_2_out);
  and and_3 (and_3_out, Q2, not_1_out, not_2_out);
  or or_1 (or_1_out, and_2_out, and_3_out);
  or or_2 (R3, and_1_out, or_1_out);
endmodule

module S2_Simplificado (
  input  Q3,
  input  Q2,
  input  Q1,
  input  Q0,
  input  X,
  output S2
);

  wire and_1_out, and_2_out, not_1_out, not_2_out, not_3_out, not_4_out;

  not not_1 (not_1_out, Q3);
  not not_2 (not_2_out, Q2);
  not not_3 (not_3_out, Q0);
  not not_4 (not_4_out, X);
  and and_1 (and_1_out, not_1_out, not_2_out, Q1, not_3_out);
  and and_2 (and_2_out, not_1_out, not_2_out, Q1, not_4_out);
  or or_1 (S2, and_1_out, and_2_out);
endmodule

module R2_Simplificado (
  input  Q3,
  input  Q2,
  input  Q1,
  input  Q0,
  input  X,
  output R2
);

  wire and_1_out, and_2_out, and_3_out, not_1_out, not_2_out, or_1_out;

  not not_1 (not_1_out, Q3);
  not not_2 (not_2_out, Q0);
  and and_1 (and_1_out, not_1_out, Q2, not_2_out);
  and and_2 (and_2_out, Q3, Q2, Q1, Q0);
  and and_3 (and_3_out, not_1_out, Q2, Q1, X);
  or or_1 (or_1_out, and_1_out, and_3_out);
  or or_2 (R2, or_1_out, and_2_out);
endmodule

module S1_Simplificado (
  input  Q3,
  input  Q2,
  input  Q1,
  input  Q0,
  input  X,
  output S1
);

  wire and_1_out, and_2_out, and_3_out, not_1_out, not_2_out, not_3_out, not_4_out, not_5_out, or_1_out;

  not not_1 (not_1_out, Q2);
  not not_2 (not_2_out, Q3);
  not not_3 (not_3_out, Q1);
  not not_4 (not_4_out, Q0);
  not not_5 (not_5_out, X);
  and and_1 (and_1_out, not_2_out, not_1_out, not_3_out, Q0);
  and and_2 (and_2_out, Q3, Q2, not_3_out, not_4_out);
  and and_3 (and_3_out, Q3, Q2, not_3_out, not_5_out);
  or or_1 (or_1_out, and_1_out, and_2_out);
  or or_2 (S1, or_1_out, and_3_out);
endmodule

module R1_Simplificado (
  input  Q3,
  input  Q2,
  input  Q1,
  input  Q0,
  input  X,
  output R1
);

  wire and_1_out, and_2_out, and_3_out, not_1_out, not_2_out, not_3_out, or_1_out;

  not not_1 (not_1_out, Q0);
  not not_2 (not_2_out, Q3);
  not not_3 (not_3_out, X);
  and and_1 (and_1_out, not_2_out, Q2);
  and and_2 (and_2_out, not_2_out, Q1, X);
  and and_3 (and_3_out, Q2, Q1, not_1_out, not_3_out);
  or or_1 (or_1_out, and_1_out, and_2_out);
  or or_2 (R1, or_1_out, and_3_out);
endmodule

module S0_Simplificado (
  input  Q3,
  input  Q2,
  input  Q1,
  input  Q0,
  input  X,
  output S0
);

  wire and_1_out, and_2_out, and_3_out, not_1_out, not_2_out, not_3_out, not_4_out, not_5_out, or_1_out;

  not not_1 (not_1_out, Q3);
  not not_2 (not_2_out, Q0);
  not not_3 (not_3_out, Q0);
  not not_4 (not_4_out, Q2);
  not not_5 (not_5_out, Q0);
  and and_1 (and_1_out, not_1_out, not_2_out, X);
  and and_2 (and_2_out, Q2, not_3_out, X);
  and and_3 (and_3_out, not_1_out, not_4_out, Q1, not_5_out);
  or or_1 (or_1_out, and_1_out, and_2_out);
  or or_2 (S0, or_1_out, and_3_out);
endmodule

module R0_Simplificado (
  input  Q3,
  input  Q2,
  input  Q1,
  input  Q0,
  input  X,
  output R0
);

  wire and_1_out, and_2_out, and_3_out, and_4_out, not_1_out, not_2_out, not_3_out, not_4_out, not_5_out,
       not_6_out, or_1_out, or_2_out;

  not not_1 (not_1_out, Q1);
  not not_2 (not_2_out, X);
  not not_3 (not_3_out, Q3);
  not not_4 (not_4_out, X);
  not not_5 (not_5_out, Q1);
  not not_6 (not_6_out, Q1);
  and and_1 (and_1_out, Q2, not_1_out, not_2_out);
  and and_2 (and_2_out, not_3_out, Q1, Q0, not_4_out);
  and and_3 (and_3_out, not_1_out, not_5_out, not_6_out, Q0, X);
  and and_4 (and_4_out, Q3, Q2, Q1, Q0, X);
  or or_1 (or_1_out, and_1_out, and_2_out);
  or or_2 (or_2_out, and_3_out, and_4_out);
  or or_3 (R0, or_1_out, or_2_out);
endmodule

module Z1_Simplificado (
  input  Q3,
  input  Q2,
  input  Q0,
  output Z1
);

  wire not_1_out, not_2_out;

  not not_1 (not_1_out, Q3);
  not not_2 (not_2_out, Q0);
  and and_1 (Z1, not_1_out, Q2, not_2_out);
endmodule

module Z2_Simplificado (
  input  Q3,
  input  Q2,
  input  Q1,
  input  Q0,
  output out_5
);

  wire not_1_out, not_2_out, not_3_out;

  not not_1 (not_1_out, Q3);
  not not_2 (not_2_out, Q1);
  not not_3 (not_3_out, Q0);
  and and_1 (out_5, not_1_out, Q2, not_2_out, not_3_out);
endmodule

module Z3_Simplificado (
  input  Q3,
  input  Q2,
  input  Q1,
  input  Q0,
  output Z3
);

  and and_1 (Z3, Q3, Q2, Q1, Q0);
endmodule
